# Fritzing sketch Robot (saved by Fritzing 0.9.3b)

parts:
  Part1 = Arduino Nano (Rev3.0)
  U1 = L9110 H-bridge module [part_number="L9110 H-bridge"]
  BATT1 = 4xAA Switchable Battery Pack w/Bare Wire
  M1 = DC Motor
  M2 = DC Motor

nets:
  GND: Part1.GND, U1.GND, BATT1.NEG
  N1: Part1.D5, U1.A-IA
  N2: Part1.D6, U1.A-IB
  N3: Part1.D7, U1.B-IA
  N4: Part1.D8, U1.B-IB
  N5: U1.VCC, BATT1.POS
  N6: U1.MOTOR_A-A, M2.pin_2
  N7: U1.MOTOR_A-B, M2.pin_1
  N8: U1.MOTOR_B-A, M1.pin_2
  N9: U1.MOTOR_B-B, M1.pin_1

custom parts:
  4xAA Switchable Battery Pack w/Bare Wire: 4xAA Switchable Battery Pack with Bare Wire connection
